// Logisim project Q.2.1.circ as structural Verilog: 1 circuit, main circuit main
module main (
  input  in_1,
  input  in_2,
  input  in_3,
  input  in_4,
  output A,
  output B
);

  or or_1 (A, in_3, in_4);
  or or_2 (B, in_2, in_4);

  // Notes on the sheet:
  //   2.
  //   4-2 Encoder
endmodule
