// Logisim project Q.2.2.circ as structural Verilog: 1 circuit, main circuit main
module main (
  input  A,
  input  B,
  output A0,
  output A1,
  output A2,
  output A3
);

  wire not_1_out, not_2_out;

  not not_1 (not_1_out, A);
  not not_2 (not_2_out, B);
  and and_1 (A0, not_1_out, not_2_out);
  and and_2 (A1, A, not_2_out);
  and and_3 (A2, not_1_out, B);
  and and_4 (A3, A, B);

  // Notes on the sheet:
  //   2.
  //   2-4 Decoder
endmodule
