// Logisim project Q.3.circ as structural Verilog: 1 circuit, main circuit main
module main (
  input  B0,
  input  B1,
  input  B2,
  input  B3,
  output Y0,
  output Y1,
  output Y2,
  output Y3
);

  xor xor_1 (Y0, 1'b0, B0);
  xor xor_2 (Y1, 1'b0, B1);
  xor xor_3 (Y2, 1'b0, B2);
  xor xor_4 (Y3, 1'b0, B3);

  // Notes on the sheet:
  //   3.
endmodule
